# Fritzing sketch read_P12 (saved by Fritzing 0.9.3b)

parts:
  J1 = double row female pin header, 20 pins [form="♀ (female)"]
  J2 = double row female pin header, 20 pins [form="♀ (female)"]
  R1 = Resistor [tolerance=±5% resistance=1.5k package=THT]
  Switch = Pushbutton [package=THT]

nets:
  N1: J1.pin6, R1.Pin_1, Switch.leg1
  N2: J1.pin7, Switch.leg0
  N3: J2.pin1, R1.Pin_0

notes:
  3V
  D18
  GND
  Jetson nano 40Pin
